# Fritzing sketch maquina_expendedora (saved by Fritzing 0.9.6b)
breadboards: 1

parts:
  Part1 = Arduino Mega 2560 (Rev3)
  Part2 = Thumb Joystick
  LED1 = LED - 5mm [color="Blue (430nm)" current=0.030 package="5 mm [THT]"]
  LED2 = LED - 5mm [color="Green (555nm)" current=0.030 package="5 mm [THT]"]
  LCD1 = LCD screen
  HC-SR04_Sensor_1 = HC-SR04 Ultrasonic Distance Sensor
  S1 = Pushbutton [package="[THT]"]
  R2 = Resistor [tolerance=±5% power=0.25 resistance=220 package=THT]
  R3 = Resistor [tolerance=±5% power=0.25 resistance=220 package=THT]
  R4 = Resistor [tolerance=±5% power=0.25 resistance=220 package=THT]
  R5 = Resistor [tolerance=±5% power=0.25 resistance=220 package=THT]
  R6 = Rotary Potentiometer (Small) [maximum_resistance=100kΩ package=THT]
  Mod1 = KY-015 Temperature & Humidity Sensor Module [package="Breakout board"]

nets:
  N1: Part1.A0, Part2.HORZ
  N2: Part1.A1, Part2.VERT
  N3: Part1.D13_PWM, HC-SR04_Sensor_1.ECHO
  N4: Part1.D12_PWM, LCD1.RS
  N5: Part1.D11_PWM, LCD1.E
  N6: Part1.D10_PWM, HC-SR04_Sensor_1.TRIG
  N7: Part1.D9_PWM, R4.Pin_1
  VCC: Part1.5V, Part2.VCC, LCD1.VDD, LCD1.R/W, HC-SR04_Sensor_1.VCC, S1.Pin_3, S1.Pin_4, R3.Pin_0, R5.Pin_0, R6.leg1, Mod1.-
  GND: Part1.GND, Part2.GND, LED1.cathode, LED2.cathode, LCD1.VSS, LCD1.LED-, HC-SR04_Sensor_1.GND, R5.Pin_1, R6.leg2, Mod1.S
  N8: Part1.D2_PWM, S1.Pin_1, S1.Pin_2
  N9: Part1.D3_PWM, Part2.SEL
  N10: Part1.D4_PWM, LCD1.DB6
  N11: Part1.D5_PWM, LCD1.DB5
  N12: Part1.D6_PWM, LCD1.DB4
  N13: Part1.D7_PWM, LCD1.DB7
  N14: Part1.D24, Mod1.Vin
  N15: Part1.D25, R2.Pin_1
  N16: LED1.anode, R2.Pin_0
  N17: LED2.anode, R4.Pin_0
  N18: LCD1.V0, R6.wiper
  N19: LCD1.LED+, R3.Pin_1

custom parts:
  KY-015 Temperature & Humidity Sensor Module: KY-015 temperature and humidity sensor module, provides a low-latency serial interface to measure humidity and temperature.
